# Fritzing sketch ledcloud (saved by Fritzing 0.7.11b)
perfboards: 1

parts:
  GREEN1 = LED - 5mm [color="Green (560nm)" package="5 mm [THT]"]
  RED2 = LED - 5mm [color="Red (633nm)" package="5 mm [THT]"]
  YELLOW1 = LED - 5mm [color="Yellow (585nm)" package="5 mm [THT]"]
  YELLOW2 = LED - 5mm [color="Yellow (585nm)" package="5 mm [THT]"]
  YELLOW4 = LED - 5mm [color="Yellow (592nm)" package="5 mm [THT]"]
  YELLOW3 = LED - 5mm [color="Yellow (585nm)" package="5 mm [THT]"]
  BLUE1 = LED - 5mm [color="Blue (470nm)" package="5 mm [THT]"]
  WHITE1 = LED - 5mm [color="White (6500K)" package="5 mm [THT]"]
  Arduino_Ethernet_Shield1 = Arduino Ethernet Shield
  RED1 = LED - 5mm [color="Red (633nm)" package="5 mm [THT]"]
  RGB_FLASHING = LED - 5mm [color="White (8000K)" package="5 mm [THT]"]
  RED3 = LED - 5mm [color="Red (633nm)" package="5 mm [THT]"]
  GREEN2 = LED - 5mm [color="Green (560nm)" package="5 mm [THT]"]

nets:
  N1: GREEN1.cathode, RED2.cathode, YELLOW1.cathode, YELLOW2.cathode, YELLOW4.cathode, YELLOW3.cathode, BLUE1.cathode, WHITE1.cathode, Arduino_Ethernet_Shield1.GND, RED1.cathode, RGB_FLASHING.cathode, RED3.cathode, GREEN2.cathode
  N2: GREEN1.anode, Arduino_Ethernet_Shield1.D6, GREEN2.anode
  N3: RED2.anode, Arduino_Ethernet_Shield1.D3, RED3.anode
  N4: YELLOW1.anode, YELLOW2.anode, Arduino_Ethernet_Shield1.D5
  N5: YELLOW4.anode, YELLOW3.anode, Arduino_Ethernet_Shield1.D7
  N6: BLUE1.anode, Arduino_Ethernet_Shield1.D9
  N7: WHITE1.anode, Arduino_Ethernet_Shield1.D1TX
  N8: Arduino_Ethernet_Shield1.D8, RGB_FLASHING.anode
  N9: Arduino_Ethernet_Shield1.D2, RED1.anode
